# Fritzing sketch hydroponics_schematic (saved by Fritzing 0.9.3b)
breadboards: 1

parts:
  Part2 = Adafruit AS7341
  MH-ET_Live_Minikit_for_ESP1 = MH-ET Live Minikit for ESP32
  DHT1 = DHT22 Humidity and Temperature Sensor

nets:
  GND: Part2.GND, MH-ET_Live_Minikit_for_ESP1.GND, DHT1.GND
  VCC: Part2.VCC, MH-ET_Live_Minikit_for_ESP1.3.3V, DHT1.VDD
  N1: Part2.SCL, MH-ET_Live_Minikit_for_ESP1.IO22
  N2: Part2.SDA, MH-ET_Live_Minikit_for_ESP1.IO21

notes:
  pH Meter PH-4502C
  V
  GND
  GND
  Po
  Do
  To

custom parts:
  MH-ET Live Minikit for ESP32: MH-ET Live Minikit for ESP32 ( http://mh.nodebb.com/topic/8/mh-et-live-minikit-for-esp32/2/) PCB footprint is invalid.
